# Fritzing sketch blink (saved by Fritzing 1.0.8)

parts:
  U1 = Seeed Studio XIAO ESP32C5
  R13_(on-board) = Resistor [resistance=1.5k package=THT]
  D3_USER_LED_(on-board) = LED - 5mm [color="Yellow (595nm)" package="5 mm [THT]"]

nets:
  N1: U1.3V3, R13_(on-board).Pin_0
  N2: R13_(on-board).Pin_1, D3_USER_LED_(on-board).anode
  GPIO27: D3_USER_LED_(on-board).cathode

notes:
  esp32-c5/blink
  Blinks the on-board yellow USER LED, 1 s on / 1 s off.
  The LED hangs from 3V3, so GPIO 27 sinks the current: the firmware drives it low to light it.
  Everything drawn right of U1 is on the board itself. GPIO 27 isn't on a pad; power and the serial console both come over USB-C.
  esp32-c5/blink
  Board only, powered from USB-C. Watch the yellow USER LED next to the USB socket.
  Console: idf.py -p /dev/cu.usbmodem* monitor prints LED ON / LED OFF.

custom parts:
  Seeed Studio XIAO ESP32C5: Seeed Studio XIAO ESP32-C5 — the first XIAO module with 5 GHz Wi-Fi support, marking a new milestone in the XIAO family. Built on the RISC-V architecture, it brings together 2.4 GHz and 5 GHz dual-band Wi-Fi 6, Bluetooth 5 (LE), and IEEE 802.15.4 (Zigbee, Thread) connectivity, while offering full support for IoT application protocols including Matter, HomeKit, and MQTT. With this versatile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
