# Fritzing sketch led_flash (saved by Fritzing 1.0.8)

parts:
  U1 = Seeed Studio XIAO ESP32C5
  LED1 = LED - 5mm [color="Red (633nm)" package="5 mm [THT]"]
  R1 = Resistor [resistance=330 package=THT]

nets:
  N1: U1.D0, LED1.anode
  N2: U1.GND, R1.Pin_1
  N3: LED1.cathode, R1.Pin_0

notes:
  esp32-c5/led_flash
  Flashes an external red LED on pad D0 (GPIO 1), 0.5 s on / 0.5 s off.
  Active-high: D0 sources the current.
  I = (3.3 V − 2.0 V) / 330 Ω ≈ 4 mA.
  esp32-c5/led_flash
  LED long leg (anode) to D0; short leg through 330 Ω to GND.

custom parts:
  Seeed Studio XIAO ESP32C5: Seeed Studio XIAO ESP32-C5 — the first XIAO module with 5 GHz Wi-Fi support, marking a new milestone in the XIAO family. Built on the RISC-V architecture, it brings together 2.4 GHz and 5 GHz dual-band Wi-Fi 6, Bluetooth 5 (LE), and IEEE 802.15.4 (Zigbee, Thread) connectivity, while offering full support for IoT application protocols including Matter, HomeKit, and MQTT. With this versatile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
