# Fritzing sketch srf08_range (saved by Fritzing 1.0.8)

parts:
  U1 = Seeed Studio XIAO ESP32C5
  J1 = Devantech SRF08
  R1 = Resistor [resistance=4.7k package=THT]
  R2 = Resistor [resistance=4.7k package=THT]
  C1 = Electrolytic Capacitor [capacitance=100µF voltage=16V package="0405 [SMD, electrolytic]"]
  C2 = Ceramic Capacitor [capacitance=100nF package="100 mil [THT, multilayer]"]

nets:
  N1: U1.D4, J1.2_SDA, R1.Pin_1
  N2: U1.D5, J1.3_SCL, R2.Pin_1
  N3: U1.3V3, R1.Pin_0, R2.Pin_0
  N4: U1.GND, J1.5_0V, C1.-, C2.0
  N5: U1.5V, J1.1_+5V, C1.+, C2.1

notes:
  J1 is the SRF08's 5-way connector. Harness:
  1 red, 2 yellow, 3 blue, 5 black; 4 is left
  empty and must stay that way - it is the
  PIC's MCLR line. Ring the four wires out
  against this before you apply 5 V.
  R1/R2 pull up to 3.3 V, not 5 V: the SRF08
  fits no pull-ups of its own, so nothing can
  over-volt the XIAO. Its PIC wants 0.7 x VDD
  for a high, so 3.3 V is marginal - that is
  why, if it stays quiet. C1/C2 go at the SRF08.

custom parts:
  Seeed Studio XIAO ESP32C5: Seeed Studio XIAO ESP32-C5 — the first XIAO module with 5 GHz Wi-Fi support, marking a new milestone in the XIAO family. Built on the RISC-V architecture, it brings together 2.4 GHz and 5 GHz dual-band Wi-Fi 6, Bluetooth 5 (LE), and IEEE 802.15.4 (Zigbee, Thread) connectivity, while offering full support for IoT application protocols including Matter, HomeKit, and MQTT. With this versatile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
  Devantech SRF08: Devantech SRF08 ultrasonic rangefinder: 40 kHz transducers, I2C at 5 V, default address 0xE0, 3 cm to 6 m, up to 17 echoes per ping plus a light sensor. Drawn as its 5-way connector; pin 4 (MCLR) is deliberately not connected. Schematic symbol only - this part has no breadboard or PCB view.
